# Fritzing sketch BLE (saved by Fritzing 1.0.3b)
breadboards: 1

parts:
  Componente1 = Bluetooth HC-05 Macho
  Componente2 = Arduino Uno (Rev3) - ICSP
  R2 = Resistor [tolerance=±1% resistance=1k package="0402 [SMD]"]
  R3 = Resistor [tolerance=±5% resistance=1k package="0402 [SMD]"]
  J1 = LOAD_CELL [package=1x03]
  Componente3 = HX711 Weighing Sensor Module
  R4 = Resistor [tolerance=±5% resistance=1k package="0402 [SMD]"]
  R5 = Resistor [tolerance=±5% resistance=1k package="0402 [SMD]"]
  R6 = Resistor [tolerance=±1% resistance=1k package="0402 [SMD]"]

nets:
  N1: Componente1.TXD, R3.Pin_1, R4.Pin_1
  N2: Componente1.RXD, Componente2.D11_PWM/MOSI
  VCC: Componente1.VCC, Componente2.3V3, Componente3.VCC
  GND: Componente1.GND, Componente2.GND, Componente3.GND, R5.Pin_0
  N3: Componente2.D10_PWM/SS, R3.Pin_0
  N4: Componente2.D2, Componente3.CK/TX
  N5: Componente2.D3_PWM, Componente3.DO/RX
  N6: R2.Pin_0, J1.B, Componente3.E-
  N7: R2.Pin_1, Componente3.A-, R6.Pin_1
  N8: J1.W, Componente3.A+
  N9: J1.R, Componente3.E+, R6.Pin_0
  N10: R4.Pin_0, R5.Pin_1
